// Logisim project q2_circuit.circ as structural Verilog: 1 circuit, main circuit main
module main (
  output [2:0] out_1
);

  wire and_1_out, and_2_out, and_3_out, and_4_out, and_5_out, and_6_out, and_7_out, and_8_out, and_9_out,
       and_10_out, clock_1_out, not_1_out, not_2_out, not_3_out, or_1_out, or_2_out, or_3_out;

  and and_1 (and_1_out, out_1[0], not_1_out);
  and and_2 (and_2_out, not_3_out, out_1[1]);
  and and_3 (and_3_out, out_1[0], out_1[1]);
  and and_4 (and_4_out, not_3_out, not_1_out);
  and and_5 (and_5_out, not_3_out, not_1_out);
  and and_6 (and_6_out, not_3_out, not_2_out);
  and and_7 (and_7_out, and_1_out, not_2_out);
  and and_8 (and_8_out, and_2_out, not_2_out);
  and and_9 (and_9_out, and_3_out, not_2_out);
  and and_10 (and_10_out, and_4_out, out_1[2]);
  or or_1 (or_1_out, and_5_out, and_6_out);
  or or_2 (or_2_out, and_7_out, and_8_out);
  or or_3 (or_3_out, and_9_out, and_10_out);
  Clock clock_1 (.out(clock_1_out));
  D_Flip_Flop C0 (.D(or_1_out), .clk(clock_1_out), .Q(out_1[0]));  // open: Qn, preset, reset
  D_Flip_Flop C1 (.D(or_2_out), .clk(clock_1_out), .Q(out_1[1]));  // open: Qn, preset, reset
  D_Flip_Flop C2 (.D(or_3_out), .clk(clock_1_out), .Q(out_1[2]));  // open: Qn, preset, reset
  not not_1 (not_1_out, out_1[1]);
  not not_2 (not_2_out, out_1[2]);
  not not_3 (not_3_out, out_1[0]);
endmodule
