// Logisim project ex3_test.circ as structural Verilog: 1 circuit, main circuit main
module main (
  output [7:0] ADD_OUT,
  output halt,
  output [7:0] REG_OUT
);

  AddMachine addmachine_1 (.halt(halt), .ADD_OUT(ADD_OUT), .REG_OUT(REG_OUT));

  // Notes on the sheet:
  //   Your AddMachine circuit must fit here!
  //   There should be no red or blue wires, and the result should not be all X's
endmodule
