// Logisim project ex3.circ as structural Verilog: 3 circuits, main circuit rot1
module rot1 (
  input  [7:0] in_1,
  output [7:0] out_2
);


  assign out_2 = {in_1[0], in_1[7:1]};

  // Notes on the sheet:
  //   PUT CIRCUITRY HERE
endmodule

module Running_LED (
  input  [7:0] INITIAL_LED,
  input  RST,
  output [7:0] OUT_LED
);

  wire clock_1_out, undriven;
  wire [7:0] multiplexer_1_out, register_1_q;

  Clock clock_1 (.out(clock_1_out));
  LED led_1 (.in(OUT_LED[7]));
  Multiplexer #(.width(8)) multiplexer_1 (.in0(OUT_LED), .in1(INITIAL_LED), .out(multiplexer_1_out), .sel(RST));
  LED led_2 (.in(OUT_LED[6]));
  Register register_1 (.D(multiplexer_1_out), .en(undriven), .clk(clock_1_out), .Q(register_1_q));  // open: clr
  LED led_3 (.in(OUT_LED[5]));
  rot1 rot1_1 (.in_1(register_1_q), .out_2(OUT_LED));
  LED led_4 (.in(OUT_LED[4]));
  LED led_5 (.in(OUT_LED[3]));
  LED led_6 (.in(OUT_LED[2]));
  LED led_7 (.in(OUT_LED[1]));
  LED led_8 (.in(OUT_LED[0]));

  // Notes on the sheet:
  //   PUT CIRCUITS HERE
endmodule

module autopause (
  input  RST,
  input  [7:0] T,
  input  clock,
  output out_4
);

  wire comparator_1_gt;
  wire [7:0] adder_1_out, multiplexer_1_out, register_1_q;

  Register register_1 (.D(multiplexer_1_out), .clk(clock), .Q(register_1_q));  // open: en, clr
  Multiplexer #(.width(8)) multiplexer_1 (.in0(adder_1_out), .in1({8{1'b0}}), .out(multiplexer_1_out), .sel(RST));
  Adder adder_1 (.a(register_1_q), .b(8'h1), .out(adder_1_out));  // open: cin, cout
  Comparator comparator_1 (.a(adder_1_out), .b(T), .gt(comparator_1_gt));  // open: eq, lt
  not not_1 (out_4, comparator_1_gt);
endmodule
