// Logisim project proj_2_2.circ as structural Verilog: 9 circuits, main circuit inst_fetch
module inst_fetch (
  input  clk,
  input  rst,
  input  control_en_i,
  input  [31:0] control_pc_i,
  input  [15:0] inst_i,
  output inst_en_o,
  output [31:0] current_pc_o,
  output [31:0] inst_addr_o,
  output [15:0] inst_o
);

  wire not_1_out, not_2_out;
  wire [31:0] adder_1_out, counter_1_q, multiplexer_1_out;

  not not_1 (not_1_out, rst);
  Adder #(.width(32)) adder_1 (.a(control_pc_i), .b(32'h1), .out(adder_1_out));  // open: cin, cout
  Counter #(.max('hffffffff), .width(32)) counter_1 (
    .clr(rst), .load(control_en_i), .up(not_1_out), .count(not_1_out), .clk(clk), .D(adder_1_out),
    .Q(counter_1_q));  // open: carry
  Multiplexer #(.width(32)) multiplexer_1 (
    .in0(counter_1_q), .in1(control_pc_i), .out(multiplexer_1_out), .sel(control_en_i));
  not not_2 (not_2_out, rst);
  Register #(.width(32)) register_1 (.D(multiplexer_1_out), .en(not_2_out), .clk(clk), .Q(current_pc_o), .clr(rst));
  not not_3 (inst_en_o, rst);

  assign inst_addr_o = current_pc_o;
  assign inst_o = inst_i;

  // Notes on the sheet:
  //   Don't touch
endmodule

module TOP (
  input  rst,
  input  clk,
  input  [15:0] inst,
  input  [31:0] mem_result,
  input  [31:0] current_pc,
  output mem_wen,
  output [31:0] mem_din,
  output mem_ren,
  output [31:0] alu_result,
  output control_en,
  output [31:0] control_pc,
  output wb_en,
  output [4:0] wb_addr,
  output [31:0] wb_data
);

  wire ALUSel, ASel, BrEq, BrLT, BrUn, BSel, WBSel;
  wire [2:0] ImmSel;
  wire [4:0] AddrA, AddrB, AddrD;
  wire [15:0] inst_o, multiplexer_1_out;
  wire [31:0] current_pc_o, DataA, Imm, multiplexer_4_out, multiplexer_5_out;

  Multiplexer #(.width(16)) multiplexer_1 (.in0(inst), .in1(16'h8000), .out(multiplexer_1_out), .sel(rst));
  Multiplexer #(.width(5)) multiplexer_2 (.in0({5{1'b0}}), .in1(AddrD), .out(wb_addr), .sel(wb_en));
  Multiplexer #(.width(32)) multiplexer_3 (.in0(mem_result), .in1(alu_result), .out(wb_data), .sel(WBSel));
  Addr_gen addr_gen_1 (.Inst(inst_o), .AddrD(AddrD), .AddrB(AddrB), .AddrA(AddrA));
  Reg_file reg_file_1 (
    .DataD(wb_data), .clk(clk), .RegWEn(wb_en), .AddrD(AddrD), .AddrA(AddrA), .AddrB(AddrB), .DataA(DataA),
    .DataB(mem_din));
  inst_fetch inst_fetch_1 (
    .clk(clk), .rst(rst), .control_en_i(control_en), .control_pc_i(alu_result), .inst_i(multiplexer_1_out),
    .current_pc_o(current_pc_o), .inst_o(inst_o));  // open: inst_en_o, inst_addr_o
  Multiplexer #(.width(32)) multiplexer_4 (.in0(DataA), .in1(current_pc), .out(multiplexer_4_out), .sel(ASel));
  Multiplexer #(.width(32)) multiplexer_5 (.in0(mem_din), .in1(Imm), .out(multiplexer_5_out), .sel(BSel));
  Control_logic control_logic_1 (
    .BrEq(BrEq), .Inst(inst_o), .BrLT(BrLT), .RegWEn(wb_en), .PCSel(control_en), .ImmSel(ImmSel),
    .ALUSel(ALUSel), .Bsel(BSel), .BrUn(BrUn), .Asel(ASel), .MemR(mem_ren), .MemW(mem_wen), .WBSel(WBSel));
  Imm_gen imm_gen_1 (.Inst(inst_o), .ImmSel(ImmSel), .Imm(Imm));
  ALU alu_1 (.A(multiplexer_4_out), .B(multiplexer_5_out), .ALUSel(ALUSel), .ALURes(alu_result));
  Branch_comp branch_comp_1 (.DataA(DataA), .DataB(mem_din), .BrUn(BrUn), .BrEq(BrEq), .BrLT(BrLT));

  assign control_pc = alu_result;

  // Other names for the same wires on the sheet: ALURes[31:0] = alu_result; DataB[31:0] = mem_din; MemR = mem_ren;
  //   MemW = mem_wen; PCSel = control_en; RegWEn = wb_en

  // Notes on the sheet:
  //   Fixed I/O
  //   Don't touch
endmodule

module testbench (
  input  rst,
  output mem_wen,
  output [31:0] mem_din,
  output mem_ren,
  output [31:0] mem_addr,
  output control_en,
  output [31:0] control_pc,
  output halt,
  output wb_en,
  output [4:0] wb_addr,
  output [31:0] wb_data
);

  wire clk, inst_en, not_1_out, not_2_out, not_3_out, not_4_out, por_1_out, rst_t;
  wire [15:0] inst, inst_i;
  wire [31:0] current_pc, inst_addr, mem_result;

  not not_1 (not_1_out, inst_i[0]);
  not not_2 (not_2_out, inst_i[1]);
  not not_3 (not_3_out, inst_i[13]);
  not not_4 (not_4_out, inst_i[14]);
  and and_1 (halt, not_1_out, not_2_out, not_3_out, not_4_out, inst_i[15]);
  Clock clock_1 (.out(clk));
  or or_1 (rst_t, rst, por_1_out);
  POR por_1 (.out(por_1_out));
  inst_fetch inst_fetch_1 (
    .clk(clk), .rst(rst_t), .control_en_i(control_en), .control_pc_i(control_pc), .inst_i(inst_i),
    .inst_en_o(inst_en), .current_pc_o(current_pc), .inst_addr_o(inst_addr), .inst_o(inst));
  TOP top_1 (
    .rst(rst_t), .clk(clk), .inst(inst), .mem_result(mem_result), .current_pc(current_pc), .mem_wen(mem_wen),
    .mem_din(mem_din), .mem_ren(mem_ren), .alu_result(mem_addr), .control_en(control_en),
    .control_pc(control_pc), .wb_en(wb_en), .wb_addr(wb_addr), .wb_data(wb_data));
  ROM #(.dataWidth(16)) rom_1 (.addr(inst_addr[7:0]), .data(inst_i));
  RAM #(.addrWidth(16), .asyncread("true"), .clearpin("true"), .dataWidth(32), .\type ("nonvolatile")) ram_1 (
    .addr(mem_addr[15:0]), .we(mem_wen), .oe(mem_ren), .clk(clk), .din(mem_din), .dout(mem_result),
    .clr(rst_t));

  // Other names for the same wires on the sheet: alu_result[31:0] = mem_addr

  // Notes on the sheet:
  //   contents of rom_1 (hex, n*v repeats v):
  //   4409 147d c011 bffd 1 1 4111 5429 c422 44b5 48 8482 8526 414c 511 c148 8000
  //   you can write any instruction in
endmodule

module Control_logic (
  input  BrEq,
  input  [15:0] Inst,
  input  BrLT,
  output RegWEn,
  output PCSel,
  output [2:0] ImmSel,
  output ALUSel,
  output Bsel,
  output BrUn,
  output Asel,
  output MemR,
  output MemW,
  output WBSel
);

  wire and_1_out, and_3_out, and_5_out, and_6_out, and_7_out, and_8_out, and_9_out, and_10_out, and_11_out,
       and_12_out, and_13_out, and_15_out, and_16_out, and_18_out, and_19_out, and_20_out, and_21_out,
       and_22_out, and_23_out, and_24_out, and_25_out, and_26_out, JR, not_1_out, not_2_out, not_3_out,
       not_4_out, not_5_out, not_6_out, not_7_out, not_8_out, not_9_out, not_10_out, not_11_out, not_12_out,
       not_13_out, not_14_out, not_15_out, not_16_out, not_17_out, not_20_out, not_21_out, not_22_out,
       not_23_out, not_24_out, not_25_out, not_26_out, not_27_out, not_28_out, or_2_out;

  not not_1 (not_1_out, Inst[0]);
  not not_2 (not_2_out, Inst[1]);
  not not_3 (not_3_out, Inst[13]);
  not not_4 (not_4_out, Inst[14]);
  not not_5 (not_5_out, Inst[15]);
  not not_6 (not_6_out, BrEq);
  not not_7 (not_7_out, BrLT);
  not not_8 (not_8_out, Inst[0]);
  not not_9 (not_9_out, Inst[1]);
  not not_10 (not_10_out, Inst[13]);
  not not_11 (not_11_out, Inst[14]);
  not not_12 (not_12_out, Inst[15]);
  not not_13 (not_13_out, Inst[0]);
  not not_14 (not_14_out, Inst[1]);
  not not_15 (not_15_out, Inst[13]);
  not not_16 (not_16_out, Inst[14]);
  not not_17 (not_17_out, Inst[15]);
  and and_1 (and_1_out, Inst[0], not_2_out, Inst[13], not_4_out, Inst[15]);
  and and_2 (MemR, not_13_out, not_14_out, not_15_out, Inst[14], not_17_out);
  and and_3 (and_3_out, Inst[0], not_2_out, not_3_out, Inst[14], Inst[15], BrEq);
  or or_1 (PCSel, and_3_out, and_1_out, JR);
  and and_4 (MemW, not_13_out, not_15_out, Inst[14], Inst[15]);
  and and_5 (and_5_out, not_8_out, Inst[1], not_10_out, not_11_out, Inst[15]);
  and and_6 (and_6_out, Inst[0], not_2_out, Inst[14], not_5_out);
  and and_7 (and_7_out, not_8_out, not_9_out, not_10_out, not_11_out, Inst[15]);
  or or_2 (or_2_out, and_7_out, and_5_out);
  and and_8 (and_8_out, Inst[0], not_2_out, not_3_out, not_5_out);
  not not_18 (Bsel, or_2_out);
  and and_9 (and_9_out, not_13_out, not_14_out, not_15_out, Inst[14], not_17_out);
  and and_10 (and_10_out, not_1_out, not_3_out, not_4_out, not_5_out);
  not not_19 (WBSel, and_9_out);
  not not_20 (not_20_out, Inst[0]);
  not not_21 (not_21_out, Inst[2]);
  not not_22 (not_22_out, Inst[3]);
  not not_23 (not_23_out, Inst[4]);
  not not_24 (not_24_out, Inst[5]);
  not not_25 (not_25_out, Inst[6]);
  not not_26 (not_26_out, Inst[13]);
  not not_27 (not_27_out, Inst[14]);
  and and_11 (and_11_out, not_2_out, not_3_out, Inst[14], Inst[15]);
  or or_3 (ImmSel[0], and_11_out, and_10_out, and_8_out, and_6_out);
  and and_12 (and_12_out, Inst[0], not_9_out, Inst[13], not_11_out, Inst[15]);
  and and_13 (and_13_out, Inst[0], not_9_out, not_10_out, Inst[14], Inst[15]);
  and and_14 (JR, not_20_out, Inst[1], not_21_out, not_22_out, not_23_out, not_24_out, not_25_out, not_26_out, not_27_out, Inst[15]);
  or or_4 (Asel, and_13_out, and_12_out);
  and and_15 (and_15_out, not_1_out, not_2_out, not_3_out, Inst[14]);
  and and_16 (and_16_out, Inst[0], not_2_out, Inst[13], not_4_out, Inst[15]);
  and and_17 (ALUSel, not_8_out, Inst[1], not_10_out, not_11_out, not_12_out);
  and and_18 (and_18_out, Inst[0], not_2_out, not_3_out, Inst[14], Inst[15]);
  or or_5 (ImmSel[1], and_18_out, and_16_out, and_15_out);
  and and_19 (and_19_out, not_1_out, Inst[1], not_3_out, Inst[14], Inst[15]);
  and and_20 (and_20_out, not_1_out, not_2_out, not_3_out, not_4_out, not_5_out);
  and and_21 (and_21_out, Inst[0], not_2_out, Inst[13], not_4_out, Inst[15]);
  and and_22 (and_22_out, Inst[0], not_2_out, not_3_out, Inst[14], Inst[15]);
  or or_6 (ImmSel[2], and_22_out, and_21_out, and_20_out, and_19_out);
  and and_23 (and_23_out, not_1_out, Inst[1], not_3_out, not_4_out);
  not not_28 (not_28_out, JR);
  and and_24 (and_24_out, and_23_out, not_28_out);
  and and_25 (and_25_out, Inst[0], not_2_out, Inst[14], not_5_out);
  and and_26 (and_26_out, not_2_out, not_3_out, not_5_out);
  or or_7 (RegWEn, and_26_out, and_25_out, and_24_out);

  assign BrUn = 1'b0;
endmodule

module Imm_gen (
  input  [15:0] Inst,
  input  [2:0] ImmSel,
  output [31:0] Imm
);

  wire LUI, not_1_out, not_2_out, not_3_out, not_4_out, not_5_out;
  wire [4:0] multiplexer_2_out;
  wire [31:0] multiplexer_1_out;

  not not_1 (not_1_out, Inst[0]);
  not not_2 (not_2_out, Inst[1]);
  not not_3 (not_3_out, Inst[13]);
  not not_4 (not_4_out, Inst[14]);
  not not_5 (not_5_out, Inst[15]);
  and and_1 (LUI, Inst[0], not_2_out, Inst[13], Inst[14], not_5_out);
  Multiplexer #(.select(3), .width(32)) multiplexer_1 (
    .in0({32{1'b1}}), .in1({{27{Inst[12]}}, Inst[6:2]}), .in2({{26{Inst[5]}}, Inst[12:10], Inst[6], 2'b00}),
    .in3({{26{Inst[5]}}, Inst[12:10], Inst[6], 2'b00}), .in4({{25{Inst[8]}}, Inst[7], Inst[12:9], 2'b00}),
    .in5({{23{Inst[10]}}, Inst[9:7], Inst[12:11], Inst[5], Inst[6], 2'b00}),
    .in6({{21{Inst[12]}}, Inst[8], Inst[10:9], Inst[6], Inst[7], Inst[2], Inst[11], Inst[5:3], 1'b0}),
    .in7({{24{Inst[12]}}, Inst[6:5], Inst[2], Inst[11:10], Inst[4:3], 1'b0}), .out(multiplexer_1_out),
    .sel(ImmSel));
  Multiplexer #(.width(5)) multiplexer_2 (.in0({5{1'b0}}), .in1(5'b01100), .out(multiplexer_2_out), .sel(LUI));
  Shifter #(.width(32)) shifter_1 (.in(multiplexer_1_out), .\dist (multiplexer_2_out), .out(Imm));

  // Other names for the same wires on the sheet: CB_Imm[31:1] = {{24{Inst[12]}}, Inst[6:5], Inst[2], Inst[11:10], Inst[4:3]};
  //   CI_Imm[31:0] = {{27{Inst[12]}}, Inst[6:2]};
  //   CJ_Imm[31:1] = {{21{Inst[12]}}, Inst[8], Inst[10:9], Inst[6], Inst[7], Inst[2], Inst[11], Inst[5:3]};
  //   CIW_Imm[31:2] = {{23{Inst[10]}}, Inst[9:7], Inst[12:11], Inst[5], Inst[6]};
  //   CL_Imm[31:2] = {{26{Inst[5]}}, Inst[12:10], Inst[6]}; CS_Imm[31:2] = {{26{Inst[5]}}, Inst[12:10], Inst[6]};
  //   CSS_Imm[31:2] = {{25{Inst[8]}}, Inst[7], Inst[12:9]}
endmodule

module ALU (
  input  [31:0] A,
  input  [31:0] B,
  input  ALUSel,
  output [31:0] ALURes
);

  wire [31:0] adder_1_out, shifter_1_out;

  Adder #(.width(32)) adder_1 (.a(A), .b(B), .out(adder_1_out));  // open: cin, cout
  Shifter #(.width(32)) shifter_1 (.in(A), .\dist (B[4:0]), .out(shifter_1_out));
  Multiplexer #(.width(32)) multiplexer_1 (.in0(adder_1_out), .in1(shifter_1_out), .out(ALURes), .sel(ALUSel));
endmodule

module Branch_comp (
  input  [31:0] DataA,
  input  [31:0] DataB,
  input  BrUn,
  output BrEq,
  output BrLT
);

  wire comparator_1_eq, comparator_1_lt, comparator_2_eq, comparator_2_lt;

  Comparator #(.width(32)) comparator_1 (.a(DataA), .b(DataB), .eq(comparator_1_eq), .lt(comparator_1_lt));  // open: gt
  Comparator #(.mode("unsigned"), .width(32)) comparator_2 (
    .a(DataA), .b(DataB), .eq(comparator_2_eq), .lt(comparator_2_lt));  // open: gt
  Multiplexer multiplexer_1 (.in0(comparator_1_eq), .in1(comparator_2_eq), .out(BrEq), .sel(BrUn));
  Multiplexer multiplexer_2 (.in0(comparator_1_lt), .in1(comparator_2_lt), .out(BrLT), .sel(BrUn));
endmodule

module Reg_file (
  input  [31:0] DataD,
  input  clk,
  input  RegWEn,
  input  [4:0] AddrD,
  input  [4:0] AddrA,
  input  [4:0] AddrB,
  output [31:0] DataA,
  output [31:0] DataB
);

  wire AddrD_x0, AddrD_x1, AddrD_x2, AddrD_x3, AddrD_x4, AddrD_x5, AddrD_x6, AddrD_x7, AddrD_x8, AddrD_x9,
       AddrD_x10, AddrD_x11, AddrD_x12, AddrD_x13, AddrD_x14, AddrD_x15, AddrD_x16, AddrD_x17, AddrD_x18,
       AddrD_x19, AddrD_x20, AddrD_x21, AddrD_x22, AddrD_x23, AddrD_x24, AddrD_x25, AddrD_x26, AddrD_x27,
       AddrD_x28, AddrD_x29, AddrD_x30, AddrD_x31;
  wire [31:0] Data_x0, Data_x1, Data_x2, Data_x3, Data_x4, Data_x5, Data_x6, Data_x7, Data_x8, Data_x9,
       Data_x10, Data_x11, Data_x12, Data_x13, Data_x14, Data_x15, Data_x16, Data_x17, Data_x18, Data_x19,
       Data_x20, Data_x21, Data_x22, Data_x23, Data_x24, Data_x25, Data_x26, Data_x27, Data_x28, Data_x29,
       Data_x30, Data_x31;

  Demultiplexer #(.select(5)) demultiplexer_1 (
    .out0(AddrD_x0), .out1(AddrD_x1), .out2(AddrD_x2), .out3(AddrD_x3), .out4(AddrD_x4), .out5(AddrD_x5),
    .out6(AddrD_x6), .out7(AddrD_x7), .out8(AddrD_x8), .out9(AddrD_x9), .out10(AddrD_x10), .out11(AddrD_x11),
    .out12(AddrD_x12), .out13(AddrD_x13), .out14(AddrD_x14), .out15(AddrD_x15), .out16(AddrD_x16),
    .out17(AddrD_x17), .out18(AddrD_x18), .out19(AddrD_x19), .out20(AddrD_x20), .out21(AddrD_x21),
    .out22(AddrD_x22), .out23(AddrD_x23), .out24(AddrD_x24), .out25(AddrD_x25), .out26(AddrD_x26),
    .out27(AddrD_x27), .out28(AddrD_x28), .out29(AddrD_x29), .out30(AddrD_x30), .out31(AddrD_x31),
    .in(RegWEn), .sel(AddrD));
  Register #(.width(32)) x0 (.D(DataD), .en(AddrD_x0), .clk(clk), .Q(Data_x0));  // open: clr
  Register #(.width(32)) x1 (.D(DataD), .en(AddrD_x1), .clk(clk), .Q(Data_x1));  // open: clr
  Register #(.width(32)) x2 (.D(DataD), .en(AddrD_x2), .clk(clk), .Q(Data_x2));  // open: clr
  Register #(.width(32)) x3 (.D(DataD), .en(AddrD_x3), .clk(clk), .Q(Data_x3));  // open: clr
  Register #(.width(32)) x4 (.D(DataD), .en(AddrD_x4), .clk(clk), .Q(Data_x4));  // open: clr
  Register #(.width(32)) x5 (.D(DataD), .en(AddrD_x5), .clk(clk), .Q(Data_x5));  // open: clr
  Register #(.width(32)) x6 (.D(DataD), .en(AddrD_x6), .clk(clk), .Q(Data_x6));  // open: clr
  Register #(.width(32)) x7 (.D(DataD), .en(AddrD_x7), .clk(clk), .Q(Data_x7));  // open: clr
  Register #(.width(32)) x8 (.D(DataD), .en(AddrD_x8), .clk(clk), .Q(Data_x8));  // open: clr
  Register #(.width(32)) x9 (.D(DataD), .en(AddrD_x9), .clk(clk), .Q(Data_x9));  // open: clr
  Register #(.width(32)) x10 (.D(DataD), .en(AddrD_x10), .clk(clk), .Q(Data_x10));  // open: clr
  Register #(.width(32)) x11 (.D(DataD), .en(AddrD_x11), .clk(clk), .Q(Data_x11));  // open: clr
  Register #(.width(32)) x12 (.D(DataD), .en(AddrD_x12), .clk(clk), .Q(Data_x12));  // open: clr
  Register #(.width(32)) x13 (.D(DataD), .en(AddrD_x13), .clk(clk), .Q(Data_x13));  // open: clr
  Register #(.width(32)) x14 (.D(DataD), .en(AddrD_x14), .clk(clk), .Q(Data_x14));  // open: clr
  Register #(.width(32)) x15 (.D(DataD), .en(AddrD_x15), .clk(clk), .Q(Data_x15));  // open: clr
  Register #(.width(32)) x16 (.D(DataD), .en(AddrD_x16), .clk(clk), .Q(Data_x16));  // open: clr
  Register #(.width(32)) x17 (.D(DataD), .en(AddrD_x17), .clk(clk), .Q(Data_x17));  // open: clr
  Register #(.width(32)) x18 (.D(DataD), .en(AddrD_x18), .clk(clk), .Q(Data_x18));  // open: clr
  Register #(.width(32)) x19 (.D(DataD), .en(AddrD_x19), .clk(clk), .Q(Data_x19));  // open: clr
  Register #(.width(32)) x20 (.D(DataD), .en(AddrD_x20), .clk(clk), .Q(Data_x20));  // open: clr
  Register #(.width(32)) x21 (.D(DataD), .en(AddrD_x21), .clk(clk), .Q(Data_x21));  // open: clr
  Register #(.width(32)) x22 (.D(DataD), .en(AddrD_x22), .clk(clk), .Q(Data_x22));  // open: clr
  Register #(.width(32)) x23 (.D(DataD), .en(AddrD_x23), .clk(clk), .Q(Data_x23));  // open: clr
  Register #(.width(32)) x24 (.D(DataD), .en(AddrD_x24), .clk(clk), .Q(Data_x24));  // open: clr
  Register #(.width(32)) x25 (.D(DataD), .en(AddrD_x25), .clk(clk), .Q(Data_x25));  // open: clr
  Register #(.width(32)) x26 (.D(DataD), .en(AddrD_x26), .clk(clk), .Q(Data_x26));  // open: clr
  Register #(.width(32)) x27 (.D(DataD), .en(AddrD_x27), .clk(clk), .Q(Data_x27));  // open: clr
  Register #(.width(32)) x28 (.D(DataD), .en(AddrD_x28), .clk(clk), .Q(Data_x28));  // open: clr
  Register #(.width(32)) x29 (.D(DataD), .en(AddrD_x29), .clk(clk), .Q(Data_x29));  // open: clr
  Register #(.width(32)) x30 (.D(DataD), .en(AddrD_x30), .clk(clk), .Q(Data_x30));  // open: clr
  Register #(.width(32)) x31 (.D(DataD), .en(AddrD_x31), .clk(clk), .Q(Data_x31));  // open: clr
  Multiplexer #(.select(5), .width(32)) multiplexer_1 (
    .in0(Data_x0), .in1(Data_x1), .in2(Data_x2), .in3(Data_x3), .in4(Data_x4), .in5(Data_x5), .in6(Data_x6),
    .in7(Data_x7), .in8(Data_x8), .in9(Data_x9), .in10(Data_x10), .in11(Data_x11), .in12(Data_x12),
    .in13(Data_x13), .in14(Data_x14), .in15(Data_x15), .in16(Data_x16), .in17(Data_x17), .in18(Data_x18),
    .in19(Data_x19), .in20(Data_x20), .in21(Data_x21), .in22(Data_x22), .in23(Data_x23), .in24(Data_x24),
    .in25(Data_x25), .in26(Data_x26), .in27(Data_x27), .in28(Data_x28), .in29(Data_x29), .in30(Data_x30),
    .in31(Data_x31), .out(DataA), .sel(AddrA));
  Multiplexer #(.select(5), .width(32)) multiplexer_2 (
    .in0(Data_x0), .in1(Data_x1), .in2(Data_x2), .in3(Data_x3), .in4(Data_x4), .in5(Data_x5), .in6(Data_x6),
    .in7(Data_x7), .in8(Data_x8), .in9(Data_x9), .in10(Data_x10), .in11(Data_x11), .in12(Data_x12),
    .in13(Data_x13), .in14(Data_x14), .in15(Data_x15), .in16(Data_x16), .in17(Data_x17), .in18(Data_x18),
    .in19(Data_x19), .in20(Data_x20), .in21(Data_x21), .in22(Data_x22), .in23(Data_x23), .in24(Data_x24),
    .in25(Data_x25), .in26(Data_x26), .in27(Data_x27), .in28(Data_x28), .in29(Data_x29), .in30(Data_x30),
    .in31(Data_x31), .out(DataB), .sel(AddrB));
endmodule

module Addr_gen (
  input  [15:0] Inst,
  output [4:0] AddrD,
  output [4:0] AddrB,
  output [4:0] AddrA
);

  wire and_1_out, and_3_out, and_4_out, and_6_out, and_7_out, and_10_out, and_11_out, and_12_out, and_13_out,
       and_14_out, JR, not_1_out, not_2_out, not_3_out, not_4_out, not_5_out, not_6_out, not_7_out,
       not_8_out, not_9_out, not_10_out, not_11_out, not_12_out, not_13_out, not_14_out, not_15_out,
       not_16_out, not_17_out, not_18_out, not_19_out, not_20_out, rdSel, rs1Sel0, rs1Sel1, rs2Sel0, rs2Sel1;

  not not_1 (not_1_out, Inst[0]);
  not not_2 (not_2_out, Inst[1]);
  not not_3 (not_3_out, Inst[12]);
  not not_4 (not_4_out, Inst[13]);
  not not_5 (not_5_out, Inst[14]);
  not not_6 (not_6_out, Inst[15]);
  not not_7 (not_7_out, Inst[0]);
  not not_8 (not_8_out, Inst[1]);
  not not_9 (not_9_out, Inst[12]);
  not not_10 (not_10_out, Inst[13]);
  not not_11 (not_11_out, Inst[14]);
  not not_12 (not_12_out, Inst[15]);
  and and_1 (and_1_out, Inst[0], not_8_out, Inst[13], not_11_out, Inst[15]);
  and and_2 (rs2Sel0, not_1_out, Inst[1], not_4_out, Inst[15]);
  Multiplexer #(.width(5)) multiplexer_1 (.in0(Inst[11:7]), .in1({2'b01, Inst[4:2]}), .out(AddrD), .sel(rdSel));
  Multiplexer #(.select(2), .width(5)) multiplexer_2 (
    .in0({5{1'b0}}), .in1(5'b00010), .in2(Inst[11:7]), .in3({2'b01, Inst[9:7]}), .out(AddrA),
    .sel({rs1Sel1, rs1Sel0}));
  and and_3 (and_3_out, not_7_out, not_8_out, not_10_out, Inst[14]);
  and and_4 (and_4_out, not_7_out, not_10_out, Inst[14], Inst[15]);
  and and_5 (rs2Sel1, not_1_out, not_2_out, not_4_out, Inst[14], Inst[15]);
  and and_6 (and_6_out, not_7_out, not_8_out, not_10_out, not_12_out);
  not not_13 (not_13_out, Inst[0]);
  not not_14 (not_14_out, Inst[2]);
  not not_15 (not_15_out, Inst[3]);
  not not_16 (not_16_out, Inst[4]);
  not not_17 (not_17_out, Inst[5]);
  not not_18 (not_18_out, Inst[6]);
  not not_19 (not_19_out, Inst[13]);
  not not_20 (not_20_out, Inst[14]);
  and and_7 (and_7_out, not_8_out, not_10_out, Inst[14], Inst[15]);
  or or_1 (rs1Sel0, and_7_out, and_6_out, and_4_out, and_3_out, and_1_out);
  and and_8 (JR, not_13_out, Inst[1], not_14_out, not_15_out, not_16_out, not_17_out, not_18_out, not_19_out, not_20_out, Inst[15]);
  and and_9 (rdSel, not_1_out, not_2_out, not_4_out, not_6_out);
  Multiplexer #(.select(2), .width(5)) multiplexer_3 (
    .in0({5{1'b0}}), .in1(Inst[6:2]), .in2({2'b01, Inst[4:2]}), .out(AddrB), .sel({rs2Sel1, rs2Sel0}));  // open: in3
  and and_10 (and_10_out, not_7_out, Inst[1], Inst[12], not_10_out, not_11_out);
  and and_11 (and_11_out, Inst[0], not_8_out, not_10_out, not_11_out, not_12_out);
  and and_12 (and_12_out, not_7_out, Inst[1], not_10_out, not_11_out, not_12_out);
  and and_13 (and_13_out, Inst[0], not_8_out, not_10_out, Inst[14], Inst[15]);
  and and_14 (and_14_out, not_7_out, not_8_out, not_10_out, Inst[14]);
  or or_2 (rs1Sel1, and_14_out, and_13_out, and_12_out, and_11_out, and_10_out, JR);
endmodule
